# Fritzing sketch pir-motion-sensor (saved by Fritzing 0.9.0b)

parts:
  PIR1 = PIR sensor
  Part1 = Espruino Pico

nets:
  N1: PIR1.VDD, Part1.Vout
  N2: PIR1.SIG, Part1.A8
  N3: PIR1.GND, Part1.3.3

custom parts:
  Espruino Pico: Espruino is an Interactive JavaScript interpreter for Microcontrollers, so you can program them quickly and easily. The Espruino Pico is a specially designed board with Espruino software pre-installed. It complements the Espruino software with masses of functionality and great battery life.
