# Fritzing sketch reed_switch (saved by Fritzing 0.9.0b)
breadboards: 1

parts:
  S1 = Reed switch [package=THT]
  R1 = Resistor [tolerance=±5% resistance=10k package="0805 [SMD]"]
  R2 = Resistor [tolerance=±5% resistance=1k package="0805 [SMD]"]
  S2 = Reed switch [package=THT]
  Espruino_Pico = Espruino Pico
  R3 = Resistor [tolerance=±5% resistance=10k package="0805 [SMD]"]
  R4 = Resistor [tolerance=±5% resistance=1k package="0805 [SMD]"]

nets:
  N1: S1.pin_1, Espruino_Pico.3.3, R3.Pin_0
  N2: S1.pin_2, R1.Pin_0, R2.Pin_0
  N3: R1.Pin_1, S2.pin_2, Espruino_Pico.GND
  N4: R2.Pin_1, Espruino_Pico.B15
  N5: S2.pin_1, R3.Pin_1, R4.Pin_1
  N6: Espruino_Pico.A8, R4.Pin_0

notes:
  pull-up
  pull-down

custom parts:
  Espruino Pico: Espruino is an Interactive JavaScript interpreter for Microcontrollers, so you can program them quickly and easily. The Espruino Pico is a specially designed board with Espruino software pre-installed. It complements the Espruino software with masses of functionality and great battery life.
